// Logisim project somadores.circ as structural Verilog
module HalfAdder (
  input  A,
  input  B,
  output Soma,
  output Cout
);

  xor xor_1 (Soma, A, B);
  and and_1 (Cout, A, B);
endmodule

module FullAdder (
  input  A,
  input  B,
  input  Cin,
  output S,
  output Cout
);

  wire halfadder_1_cout, halfadder_1_soma, halfadder_2_cout;

  HalfAdder halfadder_1 (.A(A), .B(B), .Soma(halfadder_1_soma), .Cout(halfadder_1_cout));
  HalfAdder halfadder_2 (.A(halfadder_1_soma), .B(Cin), .Soma(S), .Cout(halfadder_2_cout));
  or or_1 (Cout, halfadder_2_cout, halfadder_1_cout);
endmodule

module RippleCarryAdder (
  input  [3:0] A,
  input  [3:0] B,
  input  Cin,
  output [3:0] S,
  output Cout
);

  wire FA0_cout, FA1_cout, FA2_cout;

  FullAdder FA0 (.A(A[0]), .B(B[0]), .Cin(Cin), .S(S[0]), .Cout(FA0_cout));
  FullAdder FA1 (.A(A[1]), .B(B[1]), .Cin(FA0_cout), .S(S[1]), .Cout(FA1_cout));
  FullAdder FA2 (.A(A[2]), .B(B[2]), .Cin(FA1_cout), .S(S[2]), .Cout(FA2_cout));
  FullAdder FA3 (.A(A[3]), .B(B[3]), .Cin(FA2_cout), .S(S[3]), .Cout(Cout));
endmodule

module CarryLookaheadAdder_4bit (
  input  [3:0] A,
  input  [3:0] B,
  input  C0,
  output [3:0] S,
  output Cout
);

  wire and_5_out, and_6_out, and_7_out, and_8_out, and_9_out, and_10_out, and_11_out, and_12_out, and_13_out,
       and_14_out, C1, C2, C3, G0, G1, G2, G3, P0, P1, P2, P3;

  and and_1 (G0, A[0], B[0]);
  xor xor_1 (P0, A[0], B[0]);
  and and_2 (G1, A[1], B[1]);
  xor xor_2 (P1, A[1], B[1]);
  and and_3 (G2, A[2], B[2]);
  xor xor_3 (P2, A[2], B[2]);
  and and_4 (G3, A[3], B[3]);
  xor xor_4 (P3, A[3], B[3]);
  and and_5 (and_5_out, P0, C0);
  and and_6 (and_6_out, P1, G0);
  and and_7 (and_7_out, P1, P0, C0);
  and and_8 (and_8_out, P2, G1);
  and and_9 (and_9_out, P2, P1, G0);
  and and_10 (and_10_out, P2, P1, P0, C0);
  and and_11 (and_11_out, P3, G2);
  and and_12 (and_12_out, P3, P2, G1);
  and and_13 (and_13_out, P3, P2, P1, G0);
  and and_14 (and_14_out, P3, P2, P1, P0, C0);
  or or_1 (C1, G0, and_5_out);
  or or_2 (C2, G1, and_6_out, and_7_out);
  or or_3 (C3, G2, and_8_out, and_9_out, and_10_out);
  or or_4 (Cout, G3, and_11_out, and_12_out, and_13_out, and_14_out);
  xor xor_5 (S[0], P0, C0);
  xor xor_6 (S[1], P1, C1);
  xor xor_7 (S[2], P2, C2);
  xor xor_8 (S[3], P3, C3);

  // Other names for the same wires on the sheet: C4 = Cout

  // Notes on the sheet:
  //   Portas G e P
  //   Bloco lookahead
  //   Portas de soma
endmodule

module CarrySelectAdder (
  input  [7:0] A,
  input  [7:0] B,
  output [7:0] S,
  output Cout
);

  wire C4, Cout_0, Cout_1;
  wire [3:0] S_high_0, S_high_1;

  RippleCarryAdder ripplecarryadder_1 (.A(A[3:0]), .B(B[3:0]), .Cin(1'b0), .S(S[3:0]), .Cout(C4));
  RippleCarryAdder ripplecarryadder_2 (.A(A[7:4]), .B(B[7:4]), .Cin(1'b0), .S(S_high_0), .Cout(Cout_0));
  RippleCarryAdder ripplecarryadder_3 (.A(A[7:4]), .B(B[7:4]), .Cin(1'b1), .S(S_high_1), .Cout(Cout_1));
  Multiplexer #(.width(4)) multiplexer_1 (.in0(S_high_0), .in1(S_high_1), .out(S[7:4]), .sel(C4));
  Multiplexer multiplexer_2 (.in0(Cout_0), .in1(Cout_1), .out(Cout), .sel(C4));

  // Other names for the same wires on the sheet: A_low[3:0] = A[3:0]; A_high[3:0] = A[7:4]; B_low[3:0] = B[3:0];
  //   B_high[3:0] = B[7:4]; S_low[3:0] = S[3:0]; S_high[3:0] = S[7:4]
endmodule

module CarrySaveAdder (
  input  [3:0] A,
  input  [3:0] B,
  input  [3:0] C,
  output [3:0] S,
  output Cout
);

  wire Carry_vec_1, Carry_vec_2, Carry_vec_3, Carry_vec_4, Cout_t;
  wire [3:0] rca_A;

  or or_1 (Cout, Carry_vec_4, Cout_t);
  FullAdder FA0 (.A(A[0]), .B(B[0]), .Cin(C[0]), .S(rca_A[0]), .Cout(Carry_vec_1));
  FullAdder FA1 (.A(A[1]), .B(B[1]), .Cin(C[1]), .S(rca_A[1]), .Cout(Carry_vec_2));
  FullAdder FA2 (.A(A[2]), .B(B[2]), .Cin(C[2]), .S(rca_A[2]), .Cout(Carry_vec_3));
  FullAdder FA3 (.A(A[3]), .B(B[3]), .Cin(C[3]), .S(rca_A[3]), .Cout(Carry_vec_4));
  RippleCarryAdder ripplecarryadder_1 (
    .A(rca_A), .B({Carry_vec_3, Carry_vec_2, Carry_vec_1, 1'b0}), .Cin(1'b0), .S(S), .Cout(Cout_t));

  // Other names for the same wires on the sheet: Cc_3 = Carry_vec_4; S_csa_0 = rca_A[0]; S_csa_1 = rca_A[1];
  //   S_csa_2 = rca_A[2]; S_csa_3 = rca_A[3]; Cc_0 = Carry_vec_1;
  //   rca_B[3:1] = {Carry_vec_3, Carry_vec_2, Carry_vec_1}; Cc_1 = Carry_vec_2; Cc_2 = Carry_vec_3
endmodule

module PrefixOperator (
  input  G_hi,
  input  P_hi,
  input  G_lo,
  input  P_lo,
  output G_out,
  output P_out
);

  wire PG;

  and and_1 (PG, P_hi, G_lo);
  or or_1 (G_out, G_hi, PG);
  and and_2 (P_out, P_hi, P_lo);
endmodule

module KoggeStone8Bit (
  input  [7:0] A,
  input  [7:0] B,
  output [7:0] out_3,
  output out_4
);

  wire C1, C2, C3, C4, C5, C6, C7, G_0_1, G_0_2, G_0_3, G_0_4, G_0_5, G_0_6, G_0_7, G_1_2, G_1_3, G_1_4,
       G_1_5, G_1_6, G_1_7, G_2_4, G_2_5, G_2_6, G_2_7, P_0_0, P_0_1, P_0_2, P_0_3, P_0_4, P_0_5, P_0_6,
       P_0_7, P_1_1, P_1_2, P_1_3, P_1_4, P_1_5, P_1_6, P_1_7, P_2_2, P_2_3, P_2_4, P_2_5, P_2_6, P_2_7,
       P_3_4, P_3_5, P_3_6, P_3_7;

  and and_1 (C1, A[0], B[0]);
  xor xor_1 (P_0_0, A[0], B[0]);
  and and_2 (G_0_1, A[1], B[1]);
  xor xor_2 (P_0_1, A[1], B[1]);
  and and_3 (G_0_2, A[2], B[2]);
  xor xor_3 (P_0_2, A[2], B[2]);
  and and_4 (G_0_3, A[3], B[3]);
  xor xor_4 (P_0_3, A[3], B[3]);
  and and_5 (G_0_4, A[4], B[4]);
  xor xor_5 (P_0_4, A[4], B[4]);
  and and_6 (G_0_5, A[5], B[5]);
  xor xor_6 (P_0_5, A[5], B[5]);
  and and_7 (G_0_6, A[6], B[6]);
  xor xor_7 (P_0_6, A[6], B[6]);
  and and_8 (G_0_7, A[7], B[7]);
  xor xor_8 (P_0_7, A[7], B[7]);
  PrefixOperator PrefOp1 (.G_hi(G_0_1), .P_hi(P_0_1), .G_lo(C1), .P_lo(P_0_0), .G_out(C2), .P_out(P_1_1));
  PrefixOperator PrefOp2 (.G_hi(G_0_2), .P_hi(P_0_2), .G_lo(G_0_1), .P_lo(P_0_1), .G_out(G_1_2), .P_out(P_1_2));
  PrefixOperator PrefOp3 (.G_hi(G_0_3), .P_hi(P_0_3), .G_lo(G_0_2), .P_lo(P_0_2), .G_out(G_1_3), .P_out(P_1_3));
  PrefixOperator PrefOp4 (.G_hi(G_0_4), .P_hi(P_0_4), .G_lo(G_0_3), .P_lo(P_0_3), .G_out(G_1_4), .P_out(P_1_4));
  PrefixOperator PrefOp5 (.G_hi(G_0_5), .P_hi(P_0_5), .G_lo(G_0_4), .P_lo(P_0_4), .G_out(G_1_5), .P_out(P_1_5));
  PrefixOperator PrefOp6 (.G_hi(G_0_6), .P_hi(P_0_6), .G_lo(G_0_5), .P_lo(P_0_5), .G_out(G_1_6), .P_out(P_1_6));
  PrefixOperator PrefOp7 (.G_hi(G_0_7), .P_hi(P_0_7), .G_lo(G_0_6), .P_lo(P_0_6), .G_out(G_1_7), .P_out(P_1_7));
  PrefixOperator PrefOp22 (.G_hi(G_1_2), .P_hi(P_1_2), .G_lo(C1), .P_lo(P_0_0), .G_out(C3), .P_out(P_2_2));
  PrefixOperator PrefOp23 (.G_hi(G_1_3), .P_hi(P_1_3), .G_lo(C2), .P_lo(P_1_1), .G_out(C4), .P_out(P_2_3));
  PrefixOperator PrefOp24 (.G_hi(G_1_4), .P_hi(P_1_4), .G_lo(G_1_2), .P_lo(P_1_2), .G_out(G_2_4), .P_out(P_2_4));
  PrefixOperator PrefOp25 (.G_hi(G_1_5), .P_hi(P_1_5), .G_lo(G_1_3), .P_lo(P_1_3), .G_out(G_2_5), .P_out(P_2_5));
  PrefixOperator PrefOp26 (.G_hi(G_1_6), .P_hi(P_1_6), .G_lo(G_1_4), .P_lo(P_1_4), .G_out(G_2_6), .P_out(P_2_6));
  PrefixOperator PrefOp27 (.G_hi(G_1_7), .P_hi(P_1_7), .G_lo(G_1_5), .P_lo(P_1_5), .G_out(G_2_7), .P_out(P_2_7));
  PrefixOperator PrefOp34 (.G_hi(G_2_4), .P_hi(P_2_4), .G_lo(C1), .P_lo(P_0_0), .G_out(C5), .P_out(P_3_4));
  PrefixOperator PrefOp35 (.G_hi(G_2_5), .P_hi(P_2_5), .G_lo(C2), .P_lo(P_1_1), .G_out(C6), .P_out(P_3_5));
  PrefixOperator PrefOp36 (.G_hi(G_2_6), .P_hi(P_2_6), .G_lo(C3), .P_lo(P_2_2), .G_out(C7), .P_out(P_3_6));
  PrefixOperator PrefOp37 (.G_hi(G_2_7), .P_hi(P_2_7), .G_lo(C4), .P_lo(P_2_3), .G_out(out_4), .P_out(P_3_7));
  xor xor_9 (out_3[0], 1'b0, P_0_0);
  xor xor_10 (out_3[1], C1, P_0_1);
  xor xor_11 (out_3[2], C2, P_0_2);
  xor xor_12 (out_3[3], C3, P_0_3);
  xor xor_13 (out_3[4], C4, P_0_4);
  xor xor_14 (out_3[5], C5, P_0_5);
  xor xor_15 (out_3[6], C6, P_0_6);
  xor xor_16 (out_3[7], C7, P_0_7);

  // Other names for the same wires on the sheet: G_0_0 = C1; G_1_0 = C1; G_2_0 = C1; G_3_0 = C1; G_1_1 = C2;
  //   G_2_1 = C2; G_3_1 = C2; G_2_2 = C3; G_3_2 = C3; G_2_3 = C4; G_3_3 = C4; G_3_4 = C5; G_3_5 = C6; G_3_6 = C7;
  //   Cout = out_4; G_3_7 = out_4; P_1_0 = P_0_0; P_2_0 = P_0_0; P_3_0 = P_0_0; P_2_1 = P_1_1; P_3_1 = P_1_1;
  //   P_3_2 = P_2_2; P_3_3 = P_2_3; S[7:0] = out_3; S0 = out_3[0]; S1 = out_3[1]; S2 = out_3[2]; S3 = out_3[3];
  //   S4 = out_3[4]; S5 = out_3[5]; S6 = out_3[6]; S7 = out_3[7]
endmodule
